# Fritzing sketch arduino-gprs20170306 (saved by Fritzing 0.9.2b)
circuit board: 8.01647cm x 6.29978cm
breadboards: 1

parts:
  MPU6050 = MPU-6050 Board GY-521 [form="♀ (female)" package=THT]
  BMP180 = Digital Temperature Sensor Breakout - TMP102
  part = DHT11 Humitidy and Temperature Sensor
  Arduino = Arduino Pro Mini v13
  GPS = Triple Axis Accelerometer Breakout - ADXL335
  part_2 = Round Pushbutton
  part_3 = Round Pushbutton
  part_4 = Round Pushbutton
  part_5 = Round Pushbutton
  GPRS = Triple Axis Accelerometer Breakout - ADXL335  # not connected
  part_6 = Triple Axis Accelerometer Breakout - ADXL335
  part_7 = Graphical LCD 128x64 [package=1x20]
  part_8 = Round Pushbutton

nets:
  VCC: MPU6050.pin1, BMP180.V+, part.VDD, Arduino.VCC, GPS.VCC, part_5.leg0
  GND: MPU6050.pin2, BMP180.GND, part.NULL, part.GND, Arduino.GND, GPS.GND, part_4.leg1, part_6.ST
  N1: MPU6050.pin3, BMP180.SCL, Arduino.A5
  N2: MPU6050.pin4, BMP180.SDA, Arduino.A4
  N3: part.DATA, Arduino.D2
  N4: Arduino.D11_PWM/MOSI, GPS.PPS
  N5: Arduino.D10_PWM/SS, GPS.RX
  N6: Arduino.D9_PWM, GPS.TX
  N7: Arduino.D8, part_6.ZOUT
  N8: Arduino.D7, part_6.YOUT
  N9: Arduino.D6_PWM, part_6.XOUT
  N10: Arduino.D5_PWM, part_7.DB4
  N11: part_2.leg1, part_8.leg1
  N12: part_3.leg0, part_6.GND, part_8.leg0

notes:
  in+
  in-
  out-
  out+
  GYL-BUPT-V1.0

custom parts:
  MPU-6050 Board GY-521: Acelerometro y Giroscopio MPU-6050 Board GY-521
  Digital Temperature Sensor Breakout - TMP102: Description: This is a breakout board for the incredibly small TMP102 digital temperature sensor. The TMP102 is a digital sensor (I2C a.k.a. TWI), has a resolution of 0.0625°C, and is accurate up to 0.5°C. The sensor requires very low-current, and is loaded with features. Communication with the TMP102 is achieved through a two-wire serial interface. There is no on-board voltage regulator, so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
  DHT11 Humitidy and Temperature Sensor: DHT11 Humidity and Temperature Sensor
  Triple Axis Accelerometer Breakout - ADXL335: Accelerometer for sensing three-dimensional orientation/acceleration on a breakout board. Compatible to the ADXL3xx series of sensor chips.
